# Fritzing sketch coruja_gps (saved by Fritzing 1.0.7)

parts:
  Raspberry_Pi_Pico_2_W = Raspberry Pi Pico
  GPS_NEO-M8N_(GY-GPSV3) = Generic female header - metal rounded - 4 pins [package=THT]
  Leitor_microSD_(8_pinos) = Generic female header - 8 pins [package=THT]
  Display_ST7789_240x240 = Generic female header - 8 pins [package=THT]
  Encoder_KY-040 = Generic female header - metal rounded - 5 pins [package=THT]
  JST-XH_buzzer_(painel) = Header 2 [package=jst-2-pth-kit]
  LED_RGB_catodo_comum = RGB LED (com. cathode, rgb) [color="Red (633nm)" current=0.030A package="5 mm [THT]"]
  R1_330R = Resistor [resistance=330 tolerance=±5% power=0.25W package=THT]
  R2_68R = Resistor [resistance=68 tolerance=±5% power=0.25W package=THT]
  R3_68R = Resistor [resistance=68 tolerance=±5% power=0.25W package=THT]
  R4_1k_(base_Q1) = Resistor [resistance=1k tolerance=±5% power=0.25W package=THT]
  R5_1k_(GPIO0_->_GPS_RX) = Resistor [resistance=1k tolerance=±5% power=0.25W package=THT]
  Q1_BC337_(nao_BC547) = TRANSISTOR_NPN [package=to-92]
  D1_Schottky_1N5817/1N5819 = Schottky Diode [part_number=1N5817 package="300 mil [THT]"]
  D2_1N4148_(opcional) = Diode [package=diode-1n4148]
  C1_470uF_25V_105C = Electrolytic Capacitor [capacitance=470µF voltage=35V package="200 mil [THT, electrolytic]"]
  C2_100nF_(filtro_VSYS) = Ceramic Capacitor [capacitance=100nF voltage=35V package="100 mil [THT, multilayer]"]
  C3_100nF_(debounce_CLK) = Ceramic Capacitor [capacitance=100nF voltage=35V package="100 mil [THT, multilayer]"]
  C4_100nF_(debounce_DT) = Ceramic Capacitor [capacitance=100nF voltage=35V package="100 mil [THT, multilayer]"]
  BZ1_SFM-27_(remoto) = Piezo Speaker
  Entrada_5V_(carregador_veicular) = Header 3 [package=jst-3-pth]

nets:
  N1: Raspberry_Pi_Pico_2_W.pin_1, R5_1k_(GPIO0_->_GPS_RX).Pin_0
  N2: Raspberry_Pi_Pico_2_W.pin_2, GPS_NEO-M8N_(GY-GPSV3).pin2
  N3: Raspberry_Pi_Pico_2_W.pin_3, Raspberry_Pi_Pico_2_W.pin_33, Raspberry_Pi_Pico_2_W.pin_38, Raspberry_Pi_Pico_2_W.pin_42, GPS_NEO-M8N_(GY-GPSV3).pin4, LED_RGB_catodo_comum.common_cathode, Q1_BC337_(nao_BC547).E, C1_470uF_25V_105C.-, C2_100nF_(filtro_VSYS).1, Entrada_5V_(carregador_veicular).2
  N4: Raspberry_Pi_Pico_2_W.pin_4, Encoder_KY-040.pin5, C3_100nF_(debounce_CLK).0
  N5: Raspberry_Pi_Pico_2_W.pin_5, Encoder_KY-040.pin4, C4_100nF_(debounce_DT).0
  N6: Raspberry_Pi_Pico_2_W.pin_6, Encoder_KY-040.pin3
  N7: Raspberry_Pi_Pico_2_W.pin_7, R4_1k_(base_Q1).Pin_0
  N8: Raspberry_Pi_Pico_2_W.pin_9, R1_330R.Pin_0
  N9: Raspberry_Pi_Pico_2_W.pin_10, R2_68R.Pin_0
  N10: Raspberry_Pi_Pico_2_W.pin_11, R3_68R.Pin_0
  N11: Raspberry_Pi_Pico_2_W.pin_19, Leitor_microSD_(8_pinos).pin8
  N12: Raspberry_Pi_Pico_2_W.pin_20, Display_ST7789_240x240.pin8
  N13: Raspberry_Pi_Pico_2_W.pin_21, Leitor_microSD_(8_pinos).pin4
  N14: Raspberry_Pi_Pico_2_W.pin_22, Leitor_microSD_(8_pinos).pin6
  N15: Raspberry_Pi_Pico_2_W.pin_24, Leitor_microSD_(8_pinos).pin3, Display_ST7789_240x240.pin3
  N16: Raspberry_Pi_Pico_2_W.pin_25, Leitor_microSD_(8_pinos).pin5, Display_ST7789_240x240.pin4
  N17: Raspberry_Pi_Pico_2_W.pin_26, Display_ST7789_240x240.pin7
  N18: Raspberry_Pi_Pico_2_W.pin_27, Display_ST7789_240x240.pin6
  N19: Raspberry_Pi_Pico_2_W.pin_29, Display_ST7789_240x240.pin5
  N20: Raspberry_Pi_Pico_2_W.pin_36, Leitor_microSD_(8_pinos).pin1, Display_ST7789_240x240.pin2, Encoder_KY-040.pin2
  N21: Raspberry_Pi_Pico_2_W.pin_39, D1_Schottky_1N5817/1N5819.cathode, C1_470uF_25V_105C.+, C2_100nF_(filtro_VSYS).0
  N22: GPS_NEO-M8N_(GY-GPSV3).pin1, JST-XH_buzzer_(painel).1, D2_1N4148_(opcional).C, BZ1_SFM-27_(remoto).pin1
  N23: GPS_NEO-M8N_(GY-GPSV3).pin3, R5_1k_(GPIO0_->_GPS_RX).Pin_1
  N24: Leitor_microSD_(8_pinos).pin2, Display_ST7789_240x240.pin1, Encoder_KY-040.pin1, C3_100nF_(debounce_CLK).1, C4_100nF_(debounce_DT).1
  N25: JST-XH_buzzer_(painel).2, Q1_BC337_(nao_BC547).C, D2_1N4148_(opcional).A, BZ1_SFM-27_(remoto).pin2
  N26: LED_RGB_catodo_comum.red_anode, R1_330R.Pin_1
  N27: LED_RGB_catodo_comum.green_anode, R2_68R.Pin_1
  N28: LED_RGB_catodo_comum.blue_anode, R3_68R.Pin_1
  N29: R4_1k_(base_Q1).Pin_1, Q1_BC337_(nao_BC547).B
  N30: D1_Schottky_1N5817/1N5819.anode, Entrada_5V_(carregador_veicular).1

notes:
  Rotary encoder KY-040
  Display ST7789
  adafruit 4682
  GPS NEO-M8N (GY-GPSV3)

custom parts:
  Raspberry Pi Pico: Raspberry Pi Pico. Based around the RP2040 microcontroller the Pico is a low cost microcontroller device bringing Raspberry Pi quality, cost, and easy of use to the microcontroller space. Jan 2021, Split part in to two versions: tht (this one) and SMD. This one will drill holes for a .1 in header in pcb to allow plugging in the module as well as providing pads to solder the module to the top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
